// Digital circuit HW2-2bitupdowncounter.dig as structural Verilog
module HW2_2bitupdowncounter (
  input  clk,
  input  in_6,
  input  in_7,
  output Q0,
  output Q1,
  output Q2,
  output Q3
);

  wire and_1_out, and_2_out, and_3_out, and_4_out, and_5_out, and_6_out, and_7_out, d_ff_1_nq, d_ff_2_nq,
       d_ff_3_nq, not_1_out, or_1_out, or_2_out, or_3_out, or_4_out, xor_1_out, xor_2_out, xor_3_out,
       xor_4_out;

  not not_1 (not_1_out, in_6);
  and and_1 (and_1_out, not_1_out, in_7);
  and and_2 (and_2_out, d_ff_1_nq, and_1_out);
  and and_3 (and_3_out, d_ff_2_nq, and_2_out);
  and and_4 (and_4_out, d_ff_3_nq, and_3_out);
  or or_1 (or_1_out, in_6, and_1_out);
  and and_5 (and_5_out, Q0, in_6);
  and and_6 (and_6_out, Q1, and_5_out);
  and and_7 (and_7_out, Q2, and_6_out);
  or or_2 (or_2_out, and_5_out, and_2_out);
  or or_3 (or_3_out, and_6_out, and_3_out);
  or or_4 (or_4_out, and_7_out, and_4_out);
  xor xor_1 (xor_1_out, or_1_out, Q0);
  xor xor_2 (xor_2_out, Q1, or_2_out);
  xor xor_3 (xor_3_out, Q2, or_3_out);
  xor xor_4 (xor_4_out, Q3, or_4_out);
  D_FF d_ff_1 (.D(xor_1_out), .C(clk), .Q(Q0), .nQ(d_ff_1_nq));
  D_FF d_ff_2 (.D(xor_2_out), .C(clk), .Q(Q1), .nQ(d_ff_2_nq));
  D_FF d_ff_3 (.D(xor_3_out), .C(clk), .Q(Q2), .nQ(d_ff_3_nq));
  D_FF d_ff_4 (.D(xor_4_out), .C(clk), .Q(Q3));  // open: nQ
endmodule
